# Fritzing sketch Capacitive_wheel (saved by Fritzing 0.9.2b)
circuit board: 15cm x 15cm
breadboards: 1
stripboards: 3

parts:
  Composant1 = Arduino Uno (Rev3)
  R3 = Resistor [tolerance=±5% resistance=1M package="0805 [SMD]"]
  R2 = Resistor [tolerance=±5% resistance=1M package="0805 [SMD]"]
  R1 = Resistor [tolerance=±5% resistance=1M package="0805 [SMD]"]
  C1 = Ceramic Capacitor [capacitance=100nF package="100 mil [THT, multilayer]"]
  C3 = Ceramic Capacitor [capacitance=100nF package="100 mil [THT, multilayer]"]
  C2 = Ceramic Capacitor [capacitance=100nF package="100 mil [THT, multilayer]"]

nets:
  N1: Composant1.GND, C1.0, C3.0, C2.0
  N2: Composant1.D2, R3.Pin_0, R2.Pin_0, R1.Pin_0
  N3: Composant1.D3_PWM, R1.Pin_1
  N4: Composant1.D4, R2.Pin_1
  N5: Composant1.D5_PWM, R3.Pin_1

notes:
  Copper electrodes
  1k resistors while testing because of potential electrostatic discharges
